// Logisim project PizzanTacoCPU.circ as structural Verilog: 3 circuits, main circuit main
module main (
  output [7:0] NextPC,
  output [7:0] out_2,
  output [7:0] out_3,
  output TOop,
  output [1:0] Rt,
  output WRop,
  output [1:0] Rn,
  output IMMop,
  output [6:0] imm7,
  output RMop,
  output WMop,
  output [7:0] out_12
);

  wire adder_2_out, and_1_out, and_2_out, and_3_out, and_4_out, clock_1_out, decoder_1_out0, decoder_1_out1,
       decoder_1_out2, decoder_1_out3, not_1_out, printifzero_out;
  wire [1:0] multiplexer_4_out;
  wire [7:0] alu_1_result, bit_extender_1_out, DataMemory_dout, multiplexer_1_out, multiplexer_2_out,
       multiplexer_3_out, multiplexer_5_out, register_1_q, X0_q, X1_q, X2_q, X3_q;

  Clock clock_1 (.out(clock_1_out));
  Register register_1 (.D(NextPC), .en(1'b1), .clk(clock_1_out), .Q(register_1_q));  // open: clr
  Adder adder_1 (.a(8'h1), .b(register_1_q), .out(NextPC));  // open: cin, cout
  RAM #(.dataWidth(16), .enables("line")) InstructionMemory (
    .addr(register_1_q), .we(1'b0), .clk(clock_1_out), .dout({TOop, WRop, IMMop, RMop, WMop, imm7, Rn, Rt}));  // open: din
  Decoder #(.select(2)) decoder_1 (
    .out0(decoder_1_out0), .out1(decoder_1_out1), .out2(decoder_1_out2), .out3(decoder_1_out3), .sel(Rt));  // open: en
  and and_1 (and_1_out, WRop, decoder_1_out0);
  and and_2 (and_2_out, WRop, decoder_1_out1);
  and and_3 (and_3_out, WRop, decoder_1_out2);
  and and_4 (and_4_out, WRop, decoder_1_out3);
  Register X0 (.D(out_3), .en(and_1_out), .clk(clock_1_out), .Q(X0_q));  // open: clr
  Register X1 (.D(out_3), .en(and_2_out), .clk(clock_1_out), .Q(X1_q));  // open: clr
  Register X2 (.D(out_3), .en(and_3_out), .clk(clock_1_out), .Q(X2_q));  // open: clr
  Register X3 (.D(out_3), .en(and_4_out), .clk(clock_1_out), .Q(X3_q));  // open: clr
  Multiplexer #(.width(8)) multiplexer_1 (
    .in0(multiplexer_3_out), .in1(bit_extender_1_out), .out(multiplexer_1_out), .sel(IMMop));
  assign bit_extender_1_out = {{1{1'b0}}, imm7};  // Bit_Extender bit_extender_1
  Multiplexer #(.select(2), .width(8)) multiplexer_2 (
    .in0(X0_q), .in1(X1_q), .in2(X2_q), .in3(X3_q), .out(multiplexer_2_out), .sel(Rn));
  Multiplexer #(.select(2), .width(8)) multiplexer_3 (
    .in0(X0_q), .in1(X1_q), .in2(X2_q), .in3(X3_q), .out(multiplexer_3_out), .sel(multiplexer_4_out));
  Multiplexer #(.width(2)) multiplexer_4 (.in0(imm7[6:5]), .in1(Rt), .out(multiplexer_4_out), .sel(WMop));
  ALU alu_1 (.A(multiplexer_2_out), .B(multiplexer_1_out), .upcode_TO(TOop), .RESULT(alu_1_result));
  Adder #(.width(1)) adder_2 (.a(WMop), .b(RMop), .out(adder_2_out));  // open: cin, cout
  not not_1 (not_1_out, WRop);
  RAM #(.enables("line")) DataMemory (
    .addr(alu_1_result), .we(WMop), .clk(clock_1_out), .din(multiplexer_3_out), .dout(DataMemory_dout));
  or printifzero (printifzero_out, adder_2_out, not_1_out);
  Register register_2 (.D(multiplexer_5_out), .en(1'b1), .clk(clock_1_out), .Q(out_2), .clr(1'b0));
  Multiplexer #(.width(8)) multiplexer_5 (
    .in0(alu_1_result), .in1({8{1'b0}}), .out(multiplexer_5_out), .sel(printifzero_out));
  Multiplexer #(.width(8)) multiplexer_6 (.in0(alu_1_result), .in1(DataMemory_dout), .out(out_3), .sel(RMop));
  _7_Segment_Display u_7_segment_display_1 ();  // open: g, f, a, b, e, d, c, dp
  // BCD_to_7_Segment_decoder bcd_to_7_segment_decoder_1: pin names not known
  // Binary_to_BCD_converter #(.binvalue(8)) binary_to_bcd_converter_1: pin names not known; wires that end beside it: out_2
  _7_Segment_Display u_7_segment_display_2 ();  // open: g, f, a, b, e, d, c, dp
  _7_Segment_Display u_7_segment_display_3 ();  // open: g, f, a, b, e, d, c, dp
  // BCD_to_7_Segment_decoder bcd_to_7_segment_decoder_2: pin names not known
  // BCD_to_7_Segment_decoder bcd_to_7_segment_decoder_3: pin names not known

  assign out_12 = out_3;

  // Notes on the sheet:
  //   Pizza'nTacoCPU
  //   Alice Agnoletto
  //   Write Port
  //   WriteReg
  //   RegWrite
  //   RegDataW
  //   TO
  //   WriteReg
  //   ReadMem
  //   Decoder
  //   Miguel Merlin
  //   opcode
  //   imm
  //   Instruction Memory
  //   Rt
  //   Rn
  //   imm7
  //   WriteMem
  //   clock
  //   Read Port 1
  //   MUX2
  //   RegData1
  //   ReadReg1
  //   Read Port 2
  //   RegData2
  //   ReadReg2
  //   Rm
  //   MUX1
  //   MUX3
endmodule

module ALU (
  input  [7:0] A,
  input  [7:0] B,
  input  upcode_TO,
  output [7:0] RESULT
);

  wire [7:0] adder_1_out, subtractor_1_out;

  Adder adder_1 (.a(A), .b(B), .out(adder_1_out));  // open: cin, cout
  Subtractor subtractor_1 (.a(A), .b(B), .out(subtractor_1_out));  // open: bin, bout
  Multiplexer #(.width(8)) multiplexer_1 (.in0(adder_1_out), .in1(subtractor_1_out), .out(RESULT), .sel(upcode_TO));
endmodule

module RegisterFile (
  input  clockk,
  input  [1:0] ReadReg1,
  input  [1:0] WriteReg,
  input  RegWrite,
  input  [7:0] RegDataW,
  input  [1:0] ReadReg2,
  output [7:0] RegData1,
  output [7:0] RegData2
);

  wire and_1_out, and_2_out, and_3_out, and_4_out, clock_1_out, decoder_1_out0, decoder_1_out1,
       decoder_1_out2, decoder_1_out3;
  wire [7:0] X0_q, X1_q, X2_q, X3_q;

  Decoder #(.select(2)) decoder_1 (
    .out0(decoder_1_out0), .out1(decoder_1_out1), .out2(decoder_1_out2), .out3(decoder_1_out3), .sel(WriteReg));  // open: en
  Clock clock_1 (.out(clock_1_out));
  Register X0 (.D(RegDataW), .en(and_1_out), .clk(clockk), .Q(X0_q));  // open: clr
  and and_1 (and_1_out, RegWrite, decoder_1_out0);
  Register X1 (.D(RegDataW), .en(and_2_out), .clk(clockk), .Q(X1_q));  // open: clr
  and and_2 (and_2_out, RegWrite, decoder_1_out1);
  Register X2 (.D(RegDataW), .en(and_3_out), .clk(clockk), .Q(X2_q));  // open: clr
  and and_3 (and_3_out, RegWrite, decoder_1_out2);
  Register X3 (.D(RegDataW), .en(and_4_out), .clk(clockk), .Q(X3_q));  // open: clr
  and and_4 (and_4_out, RegWrite, decoder_1_out3);
  Multiplexer #(.select(2), .width(8)) multiplexer_1 (
    .in0(X0_q), .in1(X1_q), .in2(X2_q), .in3(X3_q), .out(RegData1), .sel(ReadReg1));
  Multiplexer #(.select(2), .width(8)) multiplexer_2 (
    .in0(X0_q), .in1(X1_q), .in2(X2_q), .in3(X3_q), .out(RegData2), .sel(ReadReg2));

  // Notes on the sheet:
  //   Write Port
  //   Decoder
  //   Read Port 1
  //   Read Port 2
endmodule
